# Fritzing sketch breakbeat_sampleplayer (saved by Fritzing 0.9.6b)
breadboards: 1

parts:
  R1 = Resistor Mini [tolerance=±5% resistance=1k package=THT]
  J1 = TRRS 3.5mm Jack Breakout
  R2 = Resistor Mini [tolerance=±5% resistance=1k package=THT]
  C1 = Ceramic Capacitor [capacitance=100nF voltage=35V package="100 mil [THT, multilayer]"]
  Part1 = Adafruit ItsyBitsy RP2040 [part_number="ItsyBitsy RP2040"]

nets:
  N1: R1.Pin_0, R2.Pin_1, C1.0
  N2: R1.Pin_1, J1.RING1, J1.TIP
  GND: J1.SLEEVE, C1.1, Part1.GND
  N3: R2.Pin_0, Part1.A0
  N4: Part1.EN, Part1.D2
  N5: Part1.D3, Part1.D4, Part1.RX
  3.3V: Part1.+3V3

notes:
  TRRS adapter: https://www.sparkfun.com/products/11570
  board: ItsyBItsy RP2040 or Raspberry Pi Pico
  other parts; two 1k resistors, 0.1uF or 1uF capacitor
  breakbeat_sampleplayer breadboard layout

custom parts:
  Resistor Mini: A generic resistor (0.25W)
  Adafruit ItsyBitsy RP2040: A new chip means a new ItsyBitsy, and the Raspberry Pi RP2040 is no exception. When we saw this chip we thought "this chip is going to be awesome when we give it the ItsyBitsy teensy-weensy Treatment" and so we did! This Itsy' features the RP2040, and all niceties you know and love about the ItsyBitsy family What's smaller than a Feather but larger than a Trinket? It's an Adafruit ItsyBitsy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
