# Fritzing sketch pidaydrummachine_wiring (saved by Fritzing 0.9.6b)
breadboards: 1

parts:
  Pico = Raspberry Pi Pico
  R1 = Resistor [tolerance=±5% power=0.25 resistance=1k package=THT]
  C1 = Ceramic Capacitor [capacitance=100nF voltage=35V package="100 mil [THT, multilayer]"]
  S1 = Pushbutton [package="[THT]"]
  S2 = Pushbutton [package="[THT]"]
  S3 = Pushbutton [package="[THT]"]
  S4 = Pushbutton [package="[THT]"]
  S5 = Pushbutton [package="[THT]"]
  audiojack = TRRS 3.5mm Jack Breakout

nets:
  GND: Pico.pin_3, Pico.pin_8, Pico.pin_13, Pico.pin_18, Pico.pin_23, Pico.pin_28, Pico.pin_33, Pico.pin_38, C1.1, S1.Pin_3, S1.Pin_4, S2.Pin_3, S2.Pin_4, S3.Pin_3, S3.Pin_4, S4.Pin_3, S4.Pin_4, S5.Pin_3, S5.Pin_4, audiojack.SLEEVE
  N1: Pico.pin_20, R1.Pin_0
  N2: Pico.pin_21, S5.Pin_1, S5.Pin_2
  N3: Pico.pin_22, S4.Pin_1, S4.Pin_2
  N4: Pico.pin_24, S3.Pin_1, S3.Pin_2
  N5: Pico.pin_25, S2.Pin_1, S2.Pin_2
  N6: Pico.pin_26, S1.Pin_1, S1.Pin_2
  N7: R1.Pin_1, C1.0, audiojack.RING1, audiojack.TIP

custom parts:
  Raspberry Pi Pico: Raspberry Pi Pico. Based around the RP2040 microcontroller the Pico is a low cost microcontroller device bringing Raspberry Pi quality, cost, and easy of use to the microcontroller space. Jan 2021, Split part in to two versions: tht (this one) and SMD. This one will drill holes for a .1 in header in pcb to allow plugging in the module as well as providing pads to solder the module to the top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
