# Fritzing sketch synthio_pico_pwm (saved by Fritzing 0.9.10b)
breadboards: 1

parts:
  Pico = Raspberry Pi Pico
  TRRS = TRRS 3.5mm Jack Breakout
  C1 = Ceramic Capacitor [capacitance=100nF voltage=35V package="100 mil [THT, multilayer]"]
  C2 = Electrolytic Capacitor [capacitance=47µF voltage=35V package="100 mil [THT, electrolytic]"]
  R1 = Resistor Mini [tolerance=±5% resistance=1k package=THT]

nets:
  N1: Pico.pin_3, Pico.pin_8, Pico.pin_13, Pico.pin_18, Pico.pin_23, Pico.pin_28, Pico.pin_33, Pico.pin_38, TRRS.SLEEVE, C1.0
  N2: Pico.pin_14, R1.Pin_0
  N3: TRRS.RING1, TRRS.TIP, C2.-
  N4: C1.1, C2.+, R1.Pin_1

custom parts:
  Raspberry Pi Pico: Raspberry Pi Pico. Based around the RP2040 microcontroller the Pico is a low cost microcontroller device bringing Raspberry Pi quality, cost, and easy of use to the microcontroller space. Jan 2021, Split part in to two versions: tht (this one) and SMD. This one will drill holes for a .1 in header in pcb to allow plugging in the module as well as providing pads to solder the module to the top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
  Resistor Mini: A generic resistor (0.25W)
